# Fritzing sketch HitagiExpansionBoard (saved by Fritzing 0.9.5d)
circuit board: 10.5cm x 13.5033cm
breadboards: 1

parts:
  STEMMA = female pin header, 4 pins [form="♀ (female)"]
  BAT1 = BC9VPC [package=bc9vpc]
  POWER = Toggle Switch [package=THT]
  STEMMA1 = Adafruit Stemma 4 pin header [form="♀ (female)" package=THT]
  PWM(3) = female pin header, 3 pins [form="♀ (female)"]
  Part1 = TFT 2.2 inch 320x240 w microSD [part_number=1480]
  R8 = Resistor [tolerance=±5% resistance=330 package="0805 [SMD]"]
  Pin10 = LED - 5mm [color="Red (633nm)" package="5 mm [THT]"]
  RESET = Pushbutton [package="[SMD]"]
  SPI1 = JST PH SPI HEADER [form="♀ (female)" package=THT]
  PWM(4) = female pin header, 3 pins [form="♀ (female)"]
  Pin9 = LED - 5mm [color="Red (633nm)" package="5 mm [THT]"]
  R9 = Resistor [tolerance=±5% resistance=330 package="0805 [SMD]"]
  SPI0 = JST PH SPI HEADER [form="♀ (female)" package=THT]
  Atmega1 = ATmega644 [part_number=ATmega1284p package=pdpi]
  C1 = Ceramic Capacitor [capacitance=100nF voltage=50V package="0805 [SMD, multilayer]"]
  C2 = Ceramic Capacitor [capacitance=100nF voltage=50V package="0805 [SMD, multilayer]"]
  XTAL = Crystal [frequency="16 MHz" package=THT]
  C10 = Ceramic Capacitor [capacitance=22pF voltage=50V package="0805 [SMD, multilayer]"]
  C11 = Ceramic Capacitor [capacitance=22pF voltage=50V package="0805 [SMD, multilayer]"]
  Pin11 = LED - 5mm [color="Red (633nm)" package="5 mm [THT]"]
  R10 = Resistor [tolerance=±5% resistance=330 package="0805 [SMD]"]
  Pin12 = LED - 5mm [color="Red (633nm)" package="5 mm [THT]"]
  R11 = Resistor [tolerance=±5% resistance=330 package="0805 [SMD]"]

nets:
  AGND/ATMEGA GND/GND: STEMMA.pin1, BAT1.V-, STEMMA1.GND, PWM(3).pin1, Part1.GND, Pin10.cathode, RESET.Pin_3, RESET.Pin_4, SPI1.GND, PWM(4).pin1, Pin9.cathode, SPI0.GND, Atmega1.GND, C1.0, C2.0, C10.1, C11.1, Pin11.cathode, Pin12.cathode
  5V/ATMEGA VCC/AVCC: STEMMA.pin2, STEMMA1.V+, PWM(3).pin2, Part1.VIN, SPI1.VCC, PWM(4).pin2, SPI0.VCC, Atmega1.VCC, Atmega1.AVCC, C1.1, C2.1
  SDA: STEMMA.pin3, STEMMA1.SDA, Atmega1.PC1
  SCL: STEMMA.pin4, STEMMA1.SCL, Atmega1.PC0
  9V IN: BAT1.V+, POWER.L1
  9V: POWER.COM
  PWM0: PWM(3).pin3, Atmega1.PB3
  DC: Part1.DC, Atmega1.PC4
  LCD RESET: Part1.RESET, Atmega1.PC5
  SDCS: Part1.SDCS, Atmega1.PC3
  LCD Enable: Part1.LCDCS, Atmega1.PC2
  MOSI: Part1.MOSI, SPI1.MOSI, SPI0.MOSI, Atmega1.PB5
  MISO: Part1.MISO, SPI1.MISO, SPI0.MISO, Atmega1.PB6
  SCK: Part1.SCLK, SPI1.SCK, SPI0.SCK, Atmega1.PB7
  LED0: R8.Pin_0, Atmega1.PD4
  N1: R8.Pin_1, Pin10.anode
  RESET: RESET.Pin_1, RESET.Pin_2, Atmega1.RESET
  SPI1 Enable: SPI1.CS_, Atmega1.PC7
  PWM1: PWM(4).pin3, Atmega1.PB4
  N2: Pin9.anode, R9.Pin_1
  LED1: R9.Pin_0, Atmega1.PD5
  SPI0 Enable: SPI0.CS_, Atmega1.PC6
  XTAL2: Atmega1.XTAL2, XTAL.pin_1, C11.0
  XTAL1: Atmega1.XTAL1, XTAL.pin_0, C10.0
  LED2: Atmega1.PD6, R10.Pin_0
  LED3: Atmega1.PD7, R11.Pin_0
  AREF: Atmega1.AREF
  N3: Pin11.anode, R10.Pin_1
  N4: Pin12.anode, R11.Pin_1

notes:
  REV 5
  "Hitagi" Expansion Board
  (C) 2020 Joshua Scoggins
  CRYSTAL

custom parts:
  Adafruit Stemma 4 pin header: Adafruit STEMMA 4 pin header JST PH 4
  TFT 2.2 inch 320x240 w microSD: This lovely little display breakout is the best way to add a small, colorful and bright display to any project. Since the display uses 4-wire SPI to communicate and has its own pixel-addressable frame buffer, it can be used with every kind of microcontroller. Even a very small one with low memory and few pins available! The 2.2" display has 320x240 color pixels.
  JST PH SPI HEADER: Single device JST PH Based SPI Header
